# Fritzing sketch FanProject (saved by Fritzing 0.9.6b)
breadboards: 1

parts:
  U1 = ESP32-38PinWide [part_number=ESP32-38PinWide]
  L298N1 = L298N DC motor driver
  M1 = DC Motor
  Part1 = BME280 Breakout  # not connected
  C1 = Capacitor [package=cap-pth-small2]
  S1 = Toggle Switch spst [package=THT]
  Squix1 = OLED 0.96" 128x64 I2C SSD1306
  VCC2 = 4 x AAA Battery Mount

nets:
  GND: U1.GND, L298N1.GND, Squix1.GND, VCC2.-
  VIN: U1.VIN, Squix1.VCC
  N1: U1.GPIO16, L298N1.IN1
  N2: U1.GPIO17, L298N1.IN2
  N3: U1.GPIO19, L298N1.ENA
  N4: U1.GPIO21, Squix1.SCA
  N5: U1.GPIO22, Squix1.SCL
  N6: L298N1.OUT1, M1.pin_2, C1.2
  N7: L298N1.OUT2, M1.pin_1, C1.1
  N8: L298N1.12V, S1.COM

custom parts:
  ESP32-38PinWide: Generic 38-Pin ESP32 with wide format (only access to one side of pins on a breadboard) based on Stephen Lilley's HiLetgo ESP-WROOM-32 ESP32 ESP-32S Development Board.
  L298N DC motor driver: 2x DC motor driver with 78M05 positive voltage regulator (7..35 V) L298N: max 46 V, 2 A Set 5 V Enable jumper to enable 5 V regultor (needed for the L298N) and +5 V output at screw terminal or supply external +5 V at screw terminal Set ENA and/or ENB to +5 V to enable motor permanently or supply ENA and/or ENB with PWM signal IN1 and IN2 set rotation directory for motor A (OUT1/OUT2) IN2 and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
  Toggle Switch spst: Toggle Switch single pole single throw
